# Fritzing sketch receiver (saved by Fritzing 0.9.3b)

parts:
  Raspberry_Pi_Zero1 = Raspberry Pi Zero
  U1 = ESP8266 WiFi Module [part_number=ESP8266]

nets:
  3V3: Raspberry_Pi_Zero1.3v3, U1.VCC
  N1: Raspberry_Pi_Zero1.GPIO15, U1.TXD
  N2: Raspberry_Pi_Zero1.GPIO14, U1.RXD
  GND: Raspberry_Pi_Zero1.GND, U1.GND

custom parts:
  ESP8266 WiFi Module: Generic WiFi Module based on the ESP8266 with onboard PCB antenna and UART communications
