# Fritzing sketch receiver (saved by Fritzing 0.9.3b)

parts:
  U1 = ESP8266 WiFi Module [part_number=ESP8266]
  Raspberry_Pi_1 = Raspberry Pi 3 [part_number=RPI-3-V1.2]

nets:
  N1: U1.RXD, Raspberry_Pi_1.GIPO14
  VCC: U1.VCC, Raspberry_Pi_1.3v3
  GND: U1.GND, Raspberry_Pi_1.GND
  N2: U1.TXD, Raspberry_Pi_1.GIPO15

custom parts:
  ESP8266 WiFi Module: Generic WiFi Module based on the ESP8266 with onboard PCB antenna and UART communications
